// Logisim project controlsequence_auto.circ as structural Verilog: 15 circuits, main circuit main
// pc_out
module main (
  input  in_1,
  input  pc_reset,
  input  state_reset,
  input  in_4,
  input  adr_reset,
  input  in_6,
  input  in_7,
  input  in_8,
  input  in_9,
  output [3:0] out_10,
  output [7:0] out_11,
  output [7:0] out_12,
  output [7:0] out_13,
  output [7:0] out_14,
  output [7:0] out_15,
  output [7:0] out_16,
  output [7:0] out_17,
  output [7:0] out_18,
  output [7:0] out_19,
  output [7:0] out_20,
  output [7:0] out_21,
  output [7:0] out_22,
  output [7:0] out_23,
  output [7:0] out_24,
  output [7:0] out_25,
  output [7:0] out_26,
  output [7:0] out_27,
  output [7:0] out_28,
  output [7:0] out_29,
  output [7:0] out_30,
  output [3:0] out_31,
  output [3:0] out_32,
  output [7:0] out_33,
  output [7:0] out_34
);

  wire a_in, a_out, alu_out, b_in, b_out, c_en, hlt, ins_reg_in_en, ins_reg_out_en, load_en, mar_in_en,
       pc_en, pc_out, right_or_left, selection, shift_b, shift_out, sram_rd, sram_wr;
  wire [7:0] add_load_1_adr_out, add_load_1_adr_out_en, debug_data, multiplexer_1_out;

  Multiplexer #(.width(8)) multiplexer_1 (
    .in0(add_load_1_adr_out), .in1({out_12[7:4], out_10}), .out(multiplexer_1_out), .sel(c_en));
  add_load add_load_1 (
    .adr_en(in_1), .in_2(in_8), .adr_clk(in_6), .adr_reset(adr_reset), .in_6(in_9), .debug(in_1),
    .adr_out(add_load_1_adr_out), .adr_out_en(add_load_1_adr_out_en), .c_en(c_en), .sram_wr(sram_wr));  // open: in_5
  Hex_Digit_Display hex_digit_display_1 (.value(out_10));  // open: dp
  pc pc_1 (
    .pc_en(pc_en), .pc_clk(in_6), .pc_reset(pc_reset), .pc_load(out_10), .pc_out_en(pc_out),
    .selection(selection), .load_en(load_en), .hlt(hlt), .in_9(in_4), .pc_out(out_10));
  sram sram_1 (
    .sram_rd(sram_rd), .sram_wr(sram_wr), .sram_d_in(out_34), .mar_d_in(multiplexer_1_out),
    .mar_in_en(mar_in_en), .sram_clk(in_6), .sram_d_out({out_12[7:4], out_10}), .out_8(out_14),
    .out_9(out_15), .out_10(out_16), .out_11(out_17), .out_12(out_18), .out_13(out_19), .out_14(out_21),
    .out_15(out_22), .out_16(out_23), .out_17(out_24), .out_18(out_25), .out_19(out_26), .out_20(out_27),
    .out_21(out_28), .out_22(out_29), .out_23(out_30));
  ROM rom_1 (.addr(add_load_1_adr_out_en), .data(out_34));
  assign {out_12[7:4], out_10} = in_1 ? debug_data : 8'bz;  // Controlled_Buffer controlled_buffer_1
  reg_gp reg_gp_1 (
    .reg_in({out_12[7:4], out_10}), .reg_in_en(a_in), .reg_clk(in_6), .reg_out_en(a_out),
    .reg_int_out(out_11), .reg_out({out_12[7:4], out_10}));
  reg_gp reg_gp_2 (
    .reg_in({out_12[7:4], out_10}), .reg_in_en(b_in), .reg_clk(in_6), .reg_out_en(b_out),
    .reg_int_out(out_20), .reg_out({out_12[7:4], out_10}));
  Hex_Digit_Display hex_digit_display_2 (.value(out_11[3:0]));  // open: dp
  Hex_Digit_Display hex_digit_display_3 (.value(out_11[7:4]));  // open: dp
  Hex_Digit_Display hex_digit_display_4 (.value(out_32));  // open: dp
  ins_reg ins_reg_1 (
    .ins_reg_in({out_12[7:4], out_10}), .ins_reg_in_en(ins_reg_in_en), .clk(in_6), .reg_out(ins_reg_out_en),
    .add_outs(out_10), .ins_out(out_32));  // open: ins_reg_out_en
  Hex_Digit_Display hex_digit_display_5 (.value(out_20[7:4]));  // open: dp
  Hex_Digit_Display hex_digit_display_6 (.value(out_12[7:4]));  // open: dp
  Hex_Digit_Display hex_digit_display_7 (.value(out_20[3:0]));  // open: dp
  Hex_Digit_Display hex_digit_display_8 (.value(out_10));  // open: dp
  alu alu_1 (
    .alu_in_1(out_11), .alu_out_en(alu_out), .alu_in_2(out_20), .shift_b(shift_b),
    .right_or_left(right_or_left), .shift_out(shift_out), .alu_out({out_12[7:4], out_10}),
    .shifted_value(out_13));  // open: alu_sub, alu_carry_out
  Hex_Digit_Display hex_digit_display_9 (.value(out_13[7:4]));  // open: dp
  Hex_Digit_Display hex_digit_display_10 (.value(out_13[3:0]));  // open: dp
  control_sequence control_sequence_1 (
    .c_en(c_en), .clk(in_6), .state_reset(state_reset), .opcode(out_32), .mar_in_manual(in_1), .debug(in_1),
    .in_7(in_7), .sram_rd(sram_rd), .a_in(a_in), .b_in(b_in), .alu_out(alu_out),
    .ins_reg_in_en(ins_reg_in_en), .a_out(a_out), .b_out(b_out), .right_or_left(right_or_left),
    .pc_en(pc_en), .selection(selection), .ins_reg_out_en(ins_reg_out_en), .pc_out(pc_out),
    .mar_in_en(mar_in_en), .load_en(load_en), .hlt(hlt), .shift_b(shift_b), .shift_out(shift_out));

  assign out_12[3:0] = out_10;
  assign out_31 = out_10;
  assign out_33 = {out_12[7:4], out_10};

  // Other names for the same wires on the sheet: clk = in_6; adr_en = in_1; debug = in_1; mar_in_manual = in_1;
  //   sram_d_in[7:0] = out_34

  // Notes on the sheet:
  //   contents of rom_1 (hex, n*v repeats v):
  //   1a 2b 3b 40 50 60 70 80 90 0 c b 3
endmodule

module reg_gp (
  input  [7:0] reg_in,
  input  reg_in_en,
  input  reg_clk,
  input  reg_out_en,
  output [7:0] reg_int_out,
  output [7:0] reg_out
);

  wire multiplexer_1_out, multiplexer_2_out, multiplexer_3_out, multiplexer_4_out, multiplexer_5_out,
       multiplexer_6_out, multiplexer_7_out, multiplexer_8_out;

  Multiplexer multiplexer_1 (.in0(reg_int_out[7]), .in1(reg_in[7]), .out(multiplexer_1_out), .sel(reg_in_en));
  D_Flip_Flop d_ff_1 (.D(multiplexer_1_out), .clk(reg_clk), .Q(reg_int_out[7]));  // open: Qn, preset, reset
  assign reg_out[7] = reg_out_en ? reg_int_out[7] : 1'bz;  // Controlled_Buffer controlled_buffer_1
  Multiplexer multiplexer_2 (.in0(reg_int_out[6]), .in1(reg_in[6]), .out(multiplexer_2_out), .sel(reg_in_en));
  D_Flip_Flop d_ff_2 (.D(multiplexer_2_out), .clk(reg_clk), .Q(reg_int_out[6]));  // open: Qn, preset, reset
  Multiplexer multiplexer_3 (.in0(reg_int_out[5]), .in1(reg_in[5]), .out(multiplexer_3_out), .sel(reg_in_en));
  D_Flip_Flop d_ff_3 (.D(multiplexer_3_out), .clk(reg_clk), .Q(reg_int_out[5]));  // open: Qn, preset, reset
  assign reg_out[6] = reg_out_en ? reg_int_out[6] : 1'bz;  // Controlled_Buffer controlled_buffer_2
  Multiplexer multiplexer_4 (.in0(reg_int_out[4]), .in1(reg_in[4]), .out(multiplexer_4_out), .sel(reg_in_en));
  D_Flip_Flop d_ff_4 (.D(multiplexer_4_out), .clk(reg_clk), .Q(reg_int_out[4]));  // open: Qn, preset, reset
  assign reg_out[5] = reg_out_en ? reg_int_out[5] : 1'bz;  // Controlled_Buffer controlled_buffer_3
  Multiplexer multiplexer_5 (.in0(reg_int_out[3]), .in1(reg_in[3]), .out(multiplexer_5_out), .sel(reg_in_en));
  assign reg_out[4] = reg_out_en ? reg_int_out[4] : 1'bz;  // Controlled_Buffer controlled_buffer_4
  D_Flip_Flop d_ff_5 (.D(multiplexer_5_out), .clk(reg_clk), .Q(reg_int_out[3]));  // open: Qn, preset, reset
  assign reg_out[3] = reg_out_en ? reg_int_out[3] : 1'bz;  // Controlled_Buffer controlled_buffer_5
  Multiplexer multiplexer_6 (.in0(reg_int_out[2]), .in1(reg_in[2]), .out(multiplexer_6_out), .sel(reg_in_en));
  D_Flip_Flop d_ff_6 (.D(multiplexer_6_out), .clk(reg_clk), .Q(reg_int_out[2]));  // open: Qn, preset, reset
  Multiplexer multiplexer_7 (.in0(reg_int_out[1]), .in1(reg_in[1]), .out(multiplexer_7_out), .sel(reg_in_en));
  D_Flip_Flop d_ff_7 (.D(multiplexer_7_out), .clk(reg_clk), .Q(reg_int_out[1]));  // open: Qn, preset, reset
  assign reg_out[2] = reg_out_en ? reg_int_out[2] : 1'bz;  // Controlled_Buffer controlled_buffer_6
  Multiplexer multiplexer_8 (.in0(reg_int_out[0]), .in1(reg_in[0]), .out(multiplexer_8_out), .sel(reg_in_en));
  D_Flip_Flop d_ff_8 (.D(multiplexer_8_out), .clk(reg_clk), .Q(reg_int_out[0]));  // open: Qn, preset, reset
  assign reg_out[1] = reg_out_en ? reg_int_out[1] : 1'bz;  // Controlled_Buffer controlled_buffer_7
  assign reg_out[0] = reg_out_en ? reg_int_out[0] : 1'bz;  // Controlled_Buffer controlled_buffer_8
endmodule

module alu (
  input  [7:0] alu_in_1,
  input  alu_out_en,
  input  alu_sub,
  input  [7:0] alu_in_2,
  input  shift_b,
  input  right_or_left,
  input  shift_out,
  output [7:0] alu_out,
  output alu_carry_out,
  output [7:0] shifted_value
);

  wire adder_2_cout, adder_3_cout, adder_4_cout, adder_5_cout, adder_6_cout, adder_7_cout, adder_8_cout,
       and_1_out, and_3_out, and_4_out, and_5_out, and_6_out, and_7_out, and_8_out, and_9_out, and_10_out,
       and_11_out, and_12_out, and_14_out, multiplexer_1_out, multiplexer_2_out, multiplexer_3_out,
       multiplexer_4_out, multiplexer_5_out, multiplexer_6_out, multiplexer_7_out, multiplexer_8_out,
       not_1_out, xor_1_out, xor_2_out, xor_3_out, xor_4_out, xor_5_out, xor_6_out, xor_7_out, xor_8_out;
  wire [7:0] adder_8_out, and_2_out;

  xor xor_1 (xor_1_out, alu_in_2[7], alu_sub);
  Adder #(.width(1)) adder_1 (
    .a(alu_in_1[7]), .b(xor_1_out), .out(adder_8_out[7]), .cin(adder_2_cout), .cout(alu_carry_out));
  xor xor_2 (xor_2_out, alu_in_2[6], alu_sub);
  not not_1 (not_1_out, right_or_left);
  Adder #(.width(1)) adder_2 (
    .a(alu_in_1[6]), .b(xor_2_out), .out(adder_8_out[6]), .cin(adder_3_cout), .cout(adder_2_cout));
  xor xor_3 (xor_3_out, alu_in_2[5], alu_sub);
  Adder #(.width(1)) adder_3 (
    .a(alu_in_1[5]), .b(xor_3_out), .out(adder_8_out[5]), .cin(adder_4_cout), .cout(adder_3_cout));
  xor xor_4 (xor_4_out, alu_in_2[4], alu_sub);
  Multiplexer multiplexer_1 (.in0(alu_in_1[0]), .in1(alu_in_2[0]), .out(multiplexer_1_out), .sel(shift_b));
  and and_1 (and_1_out, multiplexer_1_out, right_or_left);
  Adder #(.width(1)) adder_4 (
    .a(alu_in_1[4]), .b(xor_4_out), .out(adder_8_out[4]), .cin(adder_5_cout), .cout(adder_4_cout));
  Multiplexer multiplexer_2 (.in0(alu_in_1[1]), .in1(alu_in_2[1]), .out(multiplexer_2_out), .sel(shift_b));
  and and_2 (and_2_out[0], not_1_out, multiplexer_2_out);
  or or_1 (and_2_out[1], and_1_out, and_4_out);
  xor xor_5 (xor_5_out, alu_in_2[3], alu_sub);
  Multiplexer multiplexer_3 (.in0(alu_in_1[2]), .in1(alu_in_2[2]), .out(multiplexer_3_out), .sel(shift_b));
  and and_3 (and_3_out, multiplexer_2_out, right_or_left);
  Adder #(.width(1)) adder_5 (
    .a(alu_in_1[3]), .b(xor_5_out), .out(adder_8_out[3]), .cin(adder_6_cout), .cout(adder_5_cout));
  xor xor_6 (xor_6_out, alu_in_2[2], alu_sub);
  and and_4 (and_4_out, not_1_out, multiplexer_3_out);
  or or_2 (and_2_out[2], and_3_out, and_6_out);
  Adder #(.width(1)) adder_6 (
    .a(alu_in_1[2]), .b(xor_6_out), .out(adder_8_out[2]), .cin(adder_7_cout), .cout(adder_6_cout));
  xor xor_7 (xor_7_out, alu_in_2[1], alu_sub);
  Multiplexer multiplexer_4 (.in0(alu_in_1[3]), .in1(alu_in_2[3]), .out(multiplexer_4_out), .sel(shift_b));
  and and_5 (and_5_out, multiplexer_3_out, right_or_left);
  and and_6 (and_6_out, not_1_out, multiplexer_4_out);
  Adder #(.width(1)) adder_7 (
    .a(alu_in_1[1]), .b(xor_7_out), .out(adder_8_out[1]), .cin(adder_8_cout), .cout(adder_7_cout));
  and and_7 (and_7_out, multiplexer_4_out, right_or_left);
  or or_3 (and_2_out[3], and_5_out, and_8_out);
  Adder #(.width(1)) adder_8 (.a(alu_in_1[0]), .b(xor_8_out), .out(adder_8_out[0]), .cin(alu_sub), .cout(adder_8_cout));
  xor xor_8 (xor_8_out, alu_in_2[0], alu_sub);
  Multiplexer multiplexer_5 (.in0(alu_in_1[4]), .in1(alu_in_2[4]), .out(multiplexer_5_out), .sel(shift_b));
  and and_8 (and_8_out, not_1_out, multiplexer_5_out);
  and and_9 (and_9_out, multiplexer_5_out, right_or_left);
  or or_4 (and_2_out[4], and_7_out, and_10_out);
  assign alu_out = alu_out_en ? adder_8_out : 8'bz;  // Controlled_Buffer controlled_buffer_1
  Multiplexer multiplexer_6 (.in0(alu_in_1[5]), .in1(alu_in_2[5]), .out(multiplexer_6_out), .sel(shift_b));
  and and_10 (and_10_out, not_1_out, multiplexer_6_out);
  and and_11 (and_11_out, multiplexer_6_out, right_or_left);
  or or_5 (and_2_out[5], and_9_out, and_12_out);
  Multiplexer multiplexer_7 (.in0(alu_in_1[6]), .in1(alu_in_2[6]), .out(multiplexer_7_out), .sel(shift_b));
  and and_12 (and_12_out, not_1_out, multiplexer_7_out);
  or or_6 (and_2_out[6], and_11_out, and_14_out);
  and and_13 (and_2_out[7], multiplexer_7_out, right_or_left);
  Multiplexer multiplexer_8 (.in0(alu_in_1[7]), .in1(alu_in_2[7]), .out(multiplexer_8_out), .sel(shift_b));
  and and_14 (and_14_out, not_1_out, multiplexer_8_out);
  assign shifted_value = shift_out ? and_2_out : 8'bz;  // Controlled_Buffer controlled_buffer_2
endmodule

module pc (
  input  pc_en,
  input  pc_clk,
  input  pc_reset,
  input  [3:0] pc_load,
  input  pc_out_en,
  input  selection,
  input  load_en,
  input  hlt,
  input  in_9,
  output [3:0] pc_out
);

  wire j_k_ff_2_qn, j_k_ff_3_qn, j_k_ff_4_qn, multiplexer_1_out, multiplexer_3_out, multiplexer_5_out;
  wire [3:0] d_ff_4_q, j_k_ff_4_q, multiplexer_2_out, multiplexer_4_out;

  Multiplexer multiplexer_1 (.in0(pc_reset), .in1(in_9), .out(multiplexer_1_out), .sel(hlt));
  J_K_Flip_Flop j_k_ff_1 (
    .J(multiplexer_3_out), .K(multiplexer_3_out), .clk(j_k_ff_2_qn), .Q(j_k_ff_4_q[3]),
    .reset(multiplexer_1_out));  // open: Qn, preset
  Multiplexer #(.width(4)) multiplexer_2 (.in1(pc_load), .out(multiplexer_2_out), .sel(load_en));  // open: in0
  J_K_Flip_Flop j_k_ff_2 (
    .J(multiplexer_3_out), .K(multiplexer_3_out), .clk(j_k_ff_3_qn), .Q(j_k_ff_4_q[2]), .Qn(j_k_ff_2_qn),
    .reset(multiplexer_1_out));  // open: preset
  J_K_Flip_Flop j_k_ff_3 (
    .J(multiplexer_3_out), .K(multiplexer_3_out), .clk(j_k_ff_4_qn), .Q(j_k_ff_4_q[1]), .Qn(j_k_ff_3_qn),
    .reset(multiplexer_1_out));  // open: preset
  J_K_Flip_Flop j_k_ff_4 (
    .J(multiplexer_3_out), .K(multiplexer_3_out), .clk(pc_clk), .Q(j_k_ff_4_q[0]), .Qn(j_k_ff_4_qn),
    .reset(multiplexer_1_out));  // open: preset
  Multiplexer multiplexer_3 (.in0(pc_en), .in1(in_9), .out(multiplexer_3_out), .sel(hlt));
  D_Flip_Flop d_ff_1 (.D(multiplexer_2_out[3]), .clk(pc_clk), .Q(d_ff_4_q[3]));  // open: Qn, preset, reset
  D_Flip_Flop d_ff_2 (.D(multiplexer_2_out[2]), .clk(pc_clk), .Q(d_ff_4_q[2]));  // open: Qn, preset, reset
  D_Flip_Flop d_ff_3 (.D(multiplexer_2_out[1]), .clk(pc_clk), .Q(d_ff_4_q[1]));  // open: Qn, preset, reset
  D_Flip_Flop d_ff_4 (.D(multiplexer_2_out[0]), .clk(pc_clk), .Q(d_ff_4_q[0]));  // open: Qn, preset, reset
  Multiplexer #(.width(4)) multiplexer_4 (.in0(j_k_ff_4_q), .in1(d_ff_4_q), .out(multiplexer_4_out), .sel(selection));
  assign pc_out = multiplexer_5_out ? multiplexer_4_out : 4'bz;  // Controlled_Buffer controlled_buffer_1
  Multiplexer multiplexer_5 (.in0(pc_out_en), .in1(in_9), .out(multiplexer_5_out), .sel(hlt));
endmodule

module dec_4x16 (
  input  [3:0] dec_sel,
  output [15:0] dec_out
);

  wire not_1_out, not_2_out, not_3_out, not_4_out;

  not not_1 (not_1_out, dec_sel[3]);
  not not_2 (not_2_out, dec_sel[2]);
  not not_3 (not_3_out, dec_sel[1]);
  not not_4 (not_4_out, dec_sel[0]);
  and and_1 (dec_out[0], not_4_out, not_3_out, not_2_out, not_1_out);
  and and_2 (dec_out[1], dec_sel[0], not_3_out, not_2_out, not_1_out);
  and and_3 (dec_out[2], not_4_out, dec_sel[1], not_2_out, not_1_out);
  and and_4 (dec_out[3], dec_sel[0], dec_sel[1], not_2_out, not_1_out);
  and and_5 (dec_out[4], not_4_out, not_3_out, dec_sel[2], not_1_out);
  and and_6 (dec_out[5], dec_sel[0], not_3_out, dec_sel[2], not_1_out);
  and and_7 (dec_out[6], not_4_out, dec_sel[1], dec_sel[2], not_1_out);
  and and_8 (dec_out[7], dec_sel[0], dec_sel[1], dec_sel[2], not_1_out);
  and and_9 (dec_out[8], not_4_out, not_3_out, not_2_out, dec_sel[3]);
  and and_10 (dec_out[9], dec_sel[0], not_3_out, not_2_out, dec_sel[3]);
  and and_11 (dec_out[10], not_4_out, dec_sel[1], not_2_out, dec_sel[3]);
  and and_12 (dec_out[11], dec_sel[0], dec_sel[1], not_2_out, dec_sel[3]);
  and and_13 (dec_out[12], not_4_out, not_3_out, dec_sel[2], dec_sel[3]);
  and and_14 (dec_out[13], dec_sel[0], not_3_out, dec_sel[2], dec_sel[3]);
  and and_15 (dec_out[14], not_4_out, dec_sel[1], dec_sel[2], dec_sel[3]);
  and and_16 (dec_out[15], dec_sel[0], dec_sel[1], dec_sel[2], dec_sel[3]);
endmodule

module sram_cell (
  input  [7:0] data_in,
  input  wr_en,
  input  clk,
  input  cs,
  input  rd_en,
  output [7:0] memory_content,
  output [7:0] data_oiut
);

  wire and_1_out, and_2_out;

  and and_1 (and_1_out, wr_en, cs);
  and and_2 (and_2_out, cs, rd_en);
  reg_gp reg_gp_1 (
    .reg_in(data_in), .reg_in_en(and_1_out), .reg_clk(clk), .reg_out_en(and_2_out),
    .reg_int_out(memory_content), .reg_out(data_oiut));
endmodule

module sram (
  input  sram_rd,
  input  sram_wr,
  input  [7:0] sram_d_in,
  input  [7:0] mar_d_in,
  input  mar_in_en,
  input  sram_clk,
  output [7:0] sram_d_out,
  output [7:0] out_8,
  output [7:0] out_9,
  output [7:0] out_10,
  output [7:0] out_11,
  output [7:0] out_12,
  output [7:0] out_13,
  output [7:0] out_14,
  output [7:0] out_15,
  output [7:0] out_16,
  output [7:0] out_17,
  output [7:0] out_18,
  output [7:0] out_19,
  output [7:0] out_20,
  output [7:0] out_21,
  output [7:0] out_22,
  output [7:0] out_23
);

  wire [7:0] controlled_buffer_1_out, reg_gp_1_reg_int_out;
  wire [15:0] dec_4x16_1_dec_out;

  reg_gp reg_gp_1 (
    .reg_in(mar_d_in), .reg_in_en(mar_in_en), .reg_clk(sram_clk), .reg_int_out(reg_gp_1_reg_int_out));  // open: reg_out_en, reg_out
  dec_4x16 dec_4x16_1 (.dec_sel(reg_gp_1_reg_int_out[3:0]), .dec_out(dec_4x16_1_dec_out));
  assign controlled_buffer_1_out = sram_wr ? sram_d_in : 8'bz;  // Controlled_Buffer controlled_buffer_1
  sram_cell sram_cell_1 (
    .data_in(controlled_buffer_1_out), .wr_en(sram_wr), .clk(sram_clk), .cs(dec_4x16_1_dec_out[0]),
    .rd_en(sram_rd), .memory_content(out_8), .data_oiut(controlled_buffer_1_out));
  sram_cell sram_cell_2 (
    .data_in(controlled_buffer_1_out), .wr_en(sram_wr), .clk(sram_clk), .cs(dec_4x16_1_dec_out[1]),
    .rd_en(sram_rd), .memory_content(out_9), .data_oiut(controlled_buffer_1_out));
  sram_cell sram_cell_3 (
    .data_in(controlled_buffer_1_out), .wr_en(sram_wr), .clk(sram_clk), .cs(dec_4x16_1_dec_out[2]),
    .rd_en(sram_rd), .memory_content(out_10), .data_oiut(controlled_buffer_1_out));
  sram_cell sram_cell_4 (
    .data_in(controlled_buffer_1_out), .wr_en(sram_wr), .clk(sram_clk), .cs(dec_4x16_1_dec_out[3]),
    .rd_en(sram_rd), .memory_content(out_11), .data_oiut(controlled_buffer_1_out));
  sram_cell sram_cell_5 (
    .data_in(controlled_buffer_1_out), .wr_en(sram_wr), .clk(sram_clk), .cs(dec_4x16_1_dec_out[4]),
    .rd_en(sram_rd), .memory_content(out_12), .data_oiut(controlled_buffer_1_out));
  sram_cell sram_cell_6 (
    .data_in(controlled_buffer_1_out), .wr_en(sram_wr), .clk(sram_clk), .cs(dec_4x16_1_dec_out[5]),
    .rd_en(sram_rd), .memory_content(out_13), .data_oiut(controlled_buffer_1_out));
  sram_cell sram_cell_7 (
    .data_in(controlled_buffer_1_out), .wr_en(sram_wr), .clk(sram_clk), .cs(dec_4x16_1_dec_out[6]),
    .rd_en(sram_rd), .memory_content(out_14), .data_oiut(controlled_buffer_1_out));
  sram_cell sram_cell_8 (
    .data_in(controlled_buffer_1_out), .wr_en(sram_wr), .clk(sram_clk), .cs(dec_4x16_1_dec_out[7]),
    .rd_en(sram_rd), .memory_content(out_15), .data_oiut(controlled_buffer_1_out));
  sram_cell sram_cell_9 (
    .data_in(controlled_buffer_1_out), .wr_en(sram_wr), .clk(sram_clk), .cs(dec_4x16_1_dec_out[8]),
    .rd_en(sram_rd), .memory_content(out_16), .data_oiut(controlled_buffer_1_out));
  sram_cell sram_cell_10 (
    .data_in(controlled_buffer_1_out), .wr_en(sram_wr), .clk(sram_clk), .cs(dec_4x16_1_dec_out[9]),
    .rd_en(sram_rd), .memory_content(out_17), .data_oiut(controlled_buffer_1_out));
  sram_cell sram_cell_11 (
    .data_in(controlled_buffer_1_out), .wr_en(sram_wr), .clk(sram_clk), .cs(dec_4x16_1_dec_out[10]),
    .rd_en(sram_rd), .memory_content(out_18), .data_oiut(controlled_buffer_1_out));
  sram_cell sram_cell_12 (
    .data_in(controlled_buffer_1_out), .wr_en(sram_wr), .clk(sram_clk), .cs(dec_4x16_1_dec_out[11]),
    .rd_en(sram_rd), .memory_content(out_19), .data_oiut(controlled_buffer_1_out));
  sram_cell sram_cell_13 (
    .data_in(controlled_buffer_1_out), .wr_en(sram_wr), .clk(sram_clk), .cs(dec_4x16_1_dec_out[12]),
    .rd_en(sram_rd), .memory_content(out_20), .data_oiut(controlled_buffer_1_out));
  sram_cell sram_cell_14 (
    .data_in(controlled_buffer_1_out), .wr_en(sram_wr), .clk(sram_clk), .cs(dec_4x16_1_dec_out[13]),
    .rd_en(sram_rd), .memory_content(out_21), .data_oiut(controlled_buffer_1_out));
  sram_cell sram_cell_15 (
    .data_in(controlled_buffer_1_out), .wr_en(sram_wr), .clk(sram_clk), .cs(dec_4x16_1_dec_out[14]),
    .rd_en(sram_rd), .memory_content(out_22), .data_oiut(controlled_buffer_1_out));
  sram_cell sram_cell_16 (
    .data_in(controlled_buffer_1_out), .wr_en(sram_wr), .clk(sram_clk), .cs(dec_4x16_1_dec_out[15]),
    .rd_en(sram_rd), .memory_content(out_23), .data_oiut(controlled_buffer_1_out));
  assign sram_d_out = sram_rd ? controlled_buffer_1_out : 8'bz;  // Controlled_Buffer controlled_buffer_2
endmodule

module ins_reg (
  input  [7:0] ins_reg_in,
  input  ins_reg_in_en,
  input  clk,
  input  reg_out,
  input  ins_reg_out_en,
  output [3:0] add_outs,
  output [3:0] ins_out
);

  wire [3:0] reg_gp_1_reg_int_out;

  reg_gp reg_gp_1 (
    .reg_in(ins_reg_in), .reg_in_en(ins_reg_in_en), .reg_clk(clk), .reg_out_en(reg_out),
    .reg_int_out({ins_out, reg_gp_1_reg_int_out}));  // open: reg_out
  assign add_outs = ins_reg_out_en ? reg_gp_1_reg_int_out : 4'bz;  // Controlled_Buffer controlled_buffer_1
endmodule

module state_counter (
  input  c_en,
  input  clk,
  input  state_reset,
  output T0,
  output T1,
  output T2,
  output T3,
  output T4
);

  wire controlled_buffer_1_out, not_1_out;
  wire [3:0] pc_1_pc_out;
  wire [15:0] dec_4x16_1_dec_out;

  assign controlled_buffer_1_out = state_reset ? state_reset : 1'bz;  // Controlled_Buffer controlled_buffer_1
  assign controlled_buffer_1_out = not_1_out ? T4 : 1'bz;  // Controlled_Buffer controlled_buffer_2
  not not_1 (not_1_out, state_reset);
  pc pc_1 (
    .pc_en(c_en), .pc_clk(clk), .pc_reset(controlled_buffer_1_out), .pc_out_en(c_en), .pc_out(pc_1_pc_out));  // open: pc_load, selection, load_en, hlt, in_9
  dec_4x16 dec_4x16_1 (
    .dec_sel(pc_1_pc_out), .dec_out({dec_4x16_1_dec_out[15:6], T4, T3, T2, T1, T0, dec_4x16_1_dec_out[0]}));
endmodule

module opcode_decoder (
  input  [3:0] opcode,
  output LDA,
  output LDB,
  output ADD,
  output SHL_A,
  output SHR_A,
  output SHL_B,
  output SHR_B,
  output JUMP,
  output HLT
);

  wire [15:0] dec_4x16_1_dec_out;

  dec_4x16 dec_4x16_1 (
    .dec_sel(opcode),
    .dec_out({dec_4x16_1_dec_out[15:10], HLT, JUMP, SHR_B, SHL_B, SHR_A, SHL_A, ADD, LDB, LDA, dec_4x16_1_dec_out[0]}));
endmodule

module control_sequence (
  input  c_en,
  input  clk,
  input  state_reset,
  input  [3:0] opcode,
  input  mar_in_manual,
  input  debug,
  input  in_7,
  output sram_rd,
  output a_in,
  output b_in,
  output alu_out,
  output ins_reg_in_en,
  output a_out,
  output b_out,
  output right_or_left,
  output pc_en,
  output selection,
  output ins_reg_out_en,
  output pc_out,
  output mar_in_en,
  output load_en,
  output hlt,
  output shift_b,
  output shift_out
);

  wire and_1_out, and_2_out, multiplexer_1_out, not_1_out, not_2_out, opcode_decoder_1_add,
       opcode_decoder_1_jump, opcode_decoder_1_lda, opcode_decoder_1_ldb, opcode_decoder_1_shl_a,
       opcode_decoder_1_shl_b, opcode_decoder_1_shr_a, opcode_decoder_1_shr_b, or_1_out, or_3_out, or_4_out,
       or_6_out, or_7_out, or_8_out, state_counter_1_t3, state_counter_1_t4;

  Multiplexer multiplexer_1 (.in0(c_en), .in1(in_7), .out(multiplexer_1_out), .sel(hlt));
  opcode_decoder opcode_decoder_1 (
    .opcode(opcode), .LDA(opcode_decoder_1_lda), .LDB(opcode_decoder_1_ldb), .ADD(opcode_decoder_1_add),
    .SHL_A(opcode_decoder_1_shl_a), .SHR_A(opcode_decoder_1_shr_a), .SHL_B(opcode_decoder_1_shl_b),
    .SHR_B(opcode_decoder_1_shr_b), .JUMP(opcode_decoder_1_jump), .HLT(hlt));
  state_counter state_counter_1 (
    .c_en(multiplexer_1_out), .clk(clk), .state_reset(state_reset), .T0(pc_out), .T1(ins_reg_in_en),
    .T2(ins_reg_out_en), .T3(state_counter_1_t3), .T4(state_counter_1_t4));
  or or_1 (or_1_out, pc_out, ins_reg_out_en);
  Multiplexer multiplexer_2 (.in0(or_1_out), .in1(mar_in_manual), .out(mar_in_en), .sel(debug));
  or or_2 (sram_rd, ins_reg_in_en, and_1_out);
  or or_3 (or_3_out, opcode_decoder_1_lda, opcode_decoder_1_ldb);
  and and_1 (and_1_out, or_3_out, state_counter_1_t3);
  not not_1 (not_1_out, opcode_decoder_1_jump);
  not not_2 (not_2_out, hlt);
  and and_2 (and_2_out, not_1_out, not_2_out);
  and and_3 (pc_en, ins_reg_in_en, and_2_out);
  and and_4 (a_in, opcode_decoder_1_lda, state_counter_1_t3);
  and and_5 (b_in, opcode_decoder_1_ldb, state_counter_1_t3);
  and and_6 (alu_out, state_counter_1_t3, opcode_decoder_1_add);
  or or_4 (or_4_out, opcode_decoder_1_shl_a, opcode_decoder_1_shr_a);
  and and_7 (a_out, state_counter_1_t3, or_4_out);
  or or_5 (shift_out, a_out, b_out);
  or or_6 (or_6_out, opcode_decoder_1_shl_b, opcode_decoder_1_shr_b);
  and and_8 (b_out, state_counter_1_t3, or_6_out);
  or or_7 (or_7_out, opcode_decoder_1_shl_a, opcode_decoder_1_shl_b);
  and and_9 (right_or_left, state_counter_1_t3, or_7_out);
  and and_10 (selection, opcode_decoder_1_jump, or_8_out);
  and and_11 (load_en, ins_reg_out_en, opcode_decoder_1_jump);
  or or_8 (or_8_out, ins_reg_out_en, pc_out);

  assign shift_b = b_out;
endmodule

module shift (
  input  [7:0] shift_in_b,
  input  [7:0] shift_in_a,
  input  shift_b,
  input  right_or_left,
  output [7:0] shifted_value
);

  wire and_1_out, and_3_out, and_4_out, and_5_out, and_6_out, and_7_out, and_8_out, and_9_out, and_10_out,
       and_11_out, and_12_out, and_14_out, multiplexer_1_out, multiplexer_2_out, multiplexer_3_out,
       multiplexer_4_out, multiplexer_5_out, multiplexer_6_out, multiplexer_7_out, multiplexer_8_out,
       not_1_out;

  not not_1 (not_1_out, right_or_left);
  Multiplexer multiplexer_1 (.in0(shift_in_a[0]), .in1(shift_in_b[0]), .out(multiplexer_1_out), .sel(shift_b));
  Multiplexer multiplexer_2 (.in0(shift_in_a[1]), .in1(shift_in_b[1]), .out(multiplexer_2_out), .sel(shift_b));
  and and_1 (and_1_out, multiplexer_1_out, right_or_left);
  and and_2 (shifted_value[0], not_1_out, multiplexer_2_out);
  and and_3 (and_3_out, multiplexer_2_out, right_or_left);
  or or_1 (shifted_value[1], and_1_out, and_4_out);
  Multiplexer multiplexer_3 (.in0(shift_in_a[2]), .in1(shift_in_b[2]), .out(multiplexer_3_out), .sel(shift_b));
  and and_4 (and_4_out, not_1_out, multiplexer_3_out);
  and and_5 (and_5_out, multiplexer_3_out, right_or_left);
  or or_2 (shifted_value[2], and_3_out, and_6_out);
  Multiplexer multiplexer_4 (.in0(shift_in_a[3]), .in1(shift_in_b[3]), .out(multiplexer_4_out), .sel(shift_b));
  and and_6 (and_6_out, not_1_out, multiplexer_4_out);
  and and_7 (and_7_out, multiplexer_4_out, right_or_left);
  or or_3 (shifted_value[3], and_5_out, and_8_out);
  Multiplexer multiplexer_5 (.in0(shift_in_a[4]), .in1(shift_in_b[4]), .out(multiplexer_5_out), .sel(shift_b));
  and and_8 (and_8_out, not_1_out, multiplexer_5_out);
  and and_9 (and_9_out, multiplexer_5_out, right_or_left);
  or or_4 (shifted_value[4], and_7_out, and_10_out);
  Multiplexer multiplexer_6 (.in0(shift_in_a[5]), .in1(shift_in_b[5]), .out(multiplexer_6_out), .sel(shift_b));
  and and_10 (and_10_out, not_1_out, multiplexer_6_out);
  or or_5 (shifted_value[5], and_9_out, and_12_out);
  Multiplexer multiplexer_7 (.in0(shift_in_a[6]), .in1(shift_in_b[6]), .out(multiplexer_7_out), .sel(shift_b));
  and and_11 (and_11_out, multiplexer_6_out, right_or_left);
  and and_12 (and_12_out, not_1_out, multiplexer_7_out);
  or or_6 (shifted_value[6], and_11_out, and_14_out);
  and and_13 (shifted_value[7], multiplexer_7_out, right_or_left);
  and and_14 (and_14_out, not_1_out, multiplexer_8_out);
  Multiplexer multiplexer_8 (.in0(shift_in_a[7]), .in1(shift_in_b[7]), .out(multiplexer_8_out), .sel(shift_b));
endmodule

module pc_not_jump (
  input  pc_en,
  input  pc_clk,
  input  pc_reset,
  input  pc_out_en,
  output [3:0] pc_out
);

  wire j_k_ff_2_qn, j_k_ff_3_qn, j_k_ff_4_qn;
  wire [3:0] j_k_ff_4_q;

  J_K_Flip_Flop j_k_ff_1 (
    .J(pc_en), .K(pc_en), .clk(j_k_ff_2_qn), .Q(j_k_ff_4_q[3]), .reset(pc_reset));  // open: Qn, preset
  J_K_Flip_Flop j_k_ff_2 (
    .J(pc_en), .K(pc_en), .clk(j_k_ff_3_qn), .Q(j_k_ff_4_q[2]), .Qn(j_k_ff_2_qn), .reset(pc_reset));  // open: preset
  J_K_Flip_Flop j_k_ff_3 (
    .J(pc_en), .K(pc_en), .clk(j_k_ff_4_qn), .Q(j_k_ff_4_q[1]), .Qn(j_k_ff_3_qn), .reset(pc_reset));  // open: preset
  J_K_Flip_Flop j_k_ff_4 (
    .J(pc_en), .K(pc_en), .clk(pc_clk), .Q(j_k_ff_4_q[0]), .Qn(j_k_ff_4_qn), .reset(pc_reset));  // open: preset
  assign pc_out = pc_out_en ? j_k_ff_4_q : 4'bz;  // Controlled_Buffer controlled_buffer_1
endmodule

module prelab (
  input  in_1,
  input  [7:0] in_2,
  input  in_3,
  input  in_4,
  input  in_5,
  input  in_6,
  input  in_7,
  input  in_8,
  input  in_9,
  input  in_10,
  input  in_11,
  input  [7:0] in_12,
  input  in_13,
  input  in_14,
  input  [7:0] in_15,
  input  in_16,
  input  in_17,
  input  in_18,
  input  [7:0] in_19,
  input  in_20,
  input  in_21,
  input  [7:0] in_22,
  output [7:0] out_23,
  output [3:0] out_24,
  output [7:0] out_25,
  output [7:0] out_26,
  output [7:0] out_27,
  output [7:0] out_28,
  output out_29
);

  wire [7:0] reg_gp_1_reg_int_out, reg_gp_1_reg_out, reg_gp_2_reg_int_out;

  reg_gp reg_gp_1 (
    .reg_in(in_2), .reg_in_en(in_3), .reg_clk(in_5), .reg_out_en(in_7), .reg_int_out(reg_gp_1_reg_int_out),
    .reg_out(reg_gp_1_reg_out));
  reg_gp reg_gp_2 (
    .reg_in(in_12), .reg_in_en(in_13), .reg_clk(in_5), .reg_out_en(in_14),
    .reg_int_out(reg_gp_2_reg_int_out), .reg_out(reg_gp_1_reg_out));
  reg_gp reg_gp_3 (
    .reg_in(in_15), .reg_in_en(in_16), .reg_clk(in_17), .reg_out_en(in_18), .reg_int_out(out_26),
    .reg_out(out_27));
  alu alu_1 (
    .alu_in_1(in_19), .alu_out_en(in_20), .alu_sub(in_21), .alu_in_2(in_22), .alu_out(out_28),
    .alu_carry_out(out_29));  // open: shift_b, right_or_left, shift_out, shifted_value
  shift shift_1 (
    .shift_in_b(reg_gp_1_reg_out), .right_or_left(in_1), .shifted_value(out_23));  // open: shift_in_a, shift_b
  alu alu_2 (
    .alu_in_1(reg_gp_1_reg_int_out), .alu_out_en(in_10), .alu_sub(in_11), .alu_in_2(reg_gp_2_reg_int_out),
    .alu_out(out_25));  // open: shift_b, right_or_left, shift_out, alu_carry_out, shifted_value
  pc pc_1 (
    .pc_en(in_4), .pc_clk(in_6), .pc_reset(in_8), .pc_out_en(in_9), .pc_out(out_24));  // open: pc_load, selection, load_en, hlt, in_9
endmodule

module add_load (
  input  adr_en,
  input  in_2,
  input  adr_clk,
  input  adr_reset,
  input  [3:0] in_5,
  input  in_6,
  input  debug,
  output [7:0] adr_out,
  output [7:0] adr_out_en,
  output c_en,
  output sram_wr
);

  wire j_k_ff_2_qn, j_k_ff_3_qn, j_k_ff_4_qn, multiplexer_1_out, multiplexer_2_out, not_1_out;

  J_K_Flip_Flop j_k_ff_1 (
    .J(multiplexer_2_out), .K(multiplexer_2_out), .clk(j_k_ff_2_qn), .Q(adr_out[3]), .reset(adr_reset));  // open: Qn, preset
  not not_1 (not_1_out, adr_clk);
  Multiplexer multiplexer_1 (.in0(debug), .in1(in_6), .out(multiplexer_1_out), .sel(c_en));
  and and_1 (sram_wr, not_1_out, multiplexer_1_out);
  J_K_Flip_Flop j_k_ff_2 (
    .J(multiplexer_2_out), .K(multiplexer_2_out), .clk(j_k_ff_3_qn), .Q(adr_out[2]), .Qn(j_k_ff_2_qn),
    .reset(adr_reset));  // open: preset
  J_K_Flip_Flop j_k_ff_3 (
    .J(multiplexer_2_out), .K(multiplexer_2_out), .clk(j_k_ff_4_qn), .Q(adr_out[1]), .Qn(j_k_ff_3_qn),
    .reset(adr_reset));  // open: preset
  J_K_Flip_Flop j_k_ff_4 (
    .J(multiplexer_2_out), .K(multiplexer_2_out), .clk(adr_clk), .Q(adr_out[0]), .Qn(j_k_ff_4_qn),
    .reset(adr_reset));  // open: preset
  Multiplexer multiplexer_2 (.in0(adr_en), .in1(in_2), .out(multiplexer_2_out), .sel(c_en));
  and and_2 (c_en, adr_out[3], adr_out[2], adr_out[0], adr_out[1]);
  Register register_1 (.D({in_5, adr_out[3:0]}), .en(adr_clk), .clk(adr_clk), .Q(adr_out_en));  // open: clr

  assign adr_out[7:4] = in_5;
endmodule
